// Logisim project FDX.circ as structural Verilog: 2 circuits, main circuit main
module main (
);

  wire and_4_out, Clock, d_ff_1_qn, isequal8_1_out_3, isequal8_2_out_3, isequal8_3_out_3, isequal8_4_out_3,
       isequal8_5_out_3, not_1_out, not_2_out, not_3_out, not_4_out, not_5_out, not_6_out, not_7_out,
       or_1_out, or_2_out, or_3_out, or_4_out, or_5_out, or_6_out, ReadWrite, SelectMen, WriteAcu, WritePC;
  wire [6:0] controlled_buffer_4_out;
  wire [7:0] Controle, controlled_buffer_3_out, IR_q, multiplexer_1_out, PC_q;
  wire [15:0] Acu_q, controlled_buffer_1_out, demultiplexer_1_out0, demultiplexer_1_out1, ram_1_data;

  Clock clock_1 (.out(Clock));
  IsEqual8 isequal8_1 (.in_1(Controle), .in_2(8'hb), .out_3(isequal8_1_out_3));
  IsEqual8 isequal8_2 (.in_1(Controle), .in_2(8'hc), .out_3(isequal8_2_out_3));
  not not_1 (not_1_out, or_1_out);
  or or_1 (or_1_out, isequal8_1_out_3, isequal8_2_out_3, isequal8_3_out_3);
  Multiplexer #(.width(8), .enable("false")) multiplexer_1 (
    .in0(PC_q), .in1(IR_q), .out(multiplexer_1_out), .sel(SelectMen));
  IsEqual8 isequal8_3 (.in_1(Controle), .in_2(8'h33), .out_3(isequal8_3_out_3));
  and and_1 (WriteAcu, or_3_out, not_4_out);
  D_Flip_Flop d_ff_1 (.clk(Clock), .D(or_2_out), .Qn(d_ff_1_qn));  // open: Q, preset, en, reset
  or or_2 (or_2_out, not_1_out, d_ff_1_qn);
  not not_2 (not_2_out, ReadWrite);
  Register #(.width(16)) IR (.D(demultiplexer_1_out0), .en(not_3_out), .Q({Controle, IR_q}), .clk(Clock));  // open: clr
  not not_3 (not_3_out, WriteAcu);
  IsEqual8 isequal8_4 (.in_1(Controle), .in_2(8'h46), .out_3(isequal8_4_out_3));
  buf or_3 (or_3_out, isequal8_1_out_3);  // OR_Gate
  not not_4 (not_4_out, d_ff_1_qn);
  assign controlled_buffer_1_out = not_5_out ? ram_1_data : 16'bz;  // Controlled_Buffer controlled_buffer_1
  RAM #(.dataWidth(16)) ram_1 (
    .addr(multiplexer_1_out), .data(ram_1_data), .clk(Clock), .ld(not_2_out));  // open: sel, clr
  assign ram_1_data = ReadWrite ? Acu_q : 16'bz;  // Controlled_Buffer controlled_buffer_2
  IsEqual8 isequal8_5 (.in_1(Controle), .in_2(8'h80), .out_3(isequal8_5_out_3));
  and and_2 (SelectMen, or_4_out, not_4_out);
  Demultiplexer #(.width(16), .enable("false")) demultiplexer_1 (
    .out0(demultiplexer_1_out0), .out1(demultiplexer_1_out1), .in(controlled_buffer_1_out), .sel(WriteAcu));
  not not_5 (not_5_out, ReadWrite);
  or or_4 (or_4_out, isequal8_1_out_3, isequal8_2_out_3);
  assign controlled_buffer_3_out = WritePC ? IR_q : 8'bz;  // Controlled_Buffer controlled_buffer_3
  Register #(.width(16)) Acu (.D(demultiplexer_1_out1), .en(WriteAcu), .Q(Acu_q), .clk(Clock));  // open: clr
  and and_3 (ReadWrite, or_5_out, not_4_out);
  not not_6 (not_6_out, WritePC);
  and and_4 (and_4_out, not_6_out, not_7_out);
  not not_7 (not_7_out, SelectMen);
  buf or_5 (or_5_out, isequal8_2_out_3);  // OR_Gate
  Counter PC (
    .load(WritePC), .D(controlled_buffer_3_out), .count(and_4_out), .Q(PC_q), .clk(Clock),
    .clr(isequal8_4_out_3));  // open: carry
  buf or_6 (or_6_out, isequal8_3_out_3);  // OR_Gate
  and and_5 (WritePC, or_6_out, not_4_out);
  assign controlled_buffer_4_out = isequal8_5_out_3 ? Acu_q[6:0] : 7'bz;  // Controlled_Buffer controlled_buffer_4
  TTY tty_1 (.data(controlled_buffer_4_out), .clk(Clock), .we(isequal8_5_out_3));  // open: clr
endmodule

module IsEqual8 (
  input  [7:0] in_1,
  input  [7:0] in_2,
  output out_3
);

  Comparator comparator_1 (.a(in_1), .b(in_2), .eq(out_3));  // open: gt, lt
endmodule
