// Logisim project MultLib.circ as structural Verilog: 1 circuit, main circuit main
module main (
  input  [7:0] In,
  input  [7:0] In_2,
  output Overflow,
  output [7:0] out_4
);

  wire and_1_out, and_2_out, and_3_out, and_4_out, and_5_out, and_6_out, and_7_out, and_8_out, and_9_out,
       and_10_out, and_11_out, and_12_out, and_13_out, and_14_out, and_15_out, and_16_out, and_17_out,
       and_18_out, and_19_out, and_20_out, and_21_out, and_22_out, and_23_out, and_24_out, and_25_out,
       and_26_out, and_27_out, and_28_out, and_29_out, and_30_out, and_31_out, and_32_out, and_33_out,
       and_34_out, and_35_out, soma1bit_1_carry_out, soma1bit_1_out, soma1bit_2_carry_out, soma1bit_2_out,
       soma1bit_3_carry_out, soma1bit_3_out, soma1bit_4_carry_out, soma1bit_4_out, soma1bit_5_carry_out,
       soma1bit_5_out, soma1bit_6_carry_out, soma1bit_6_out, soma1bit_7_carry_out, soma1bit_8_carry_out,
       soma1bit_8_out, soma1bit_9_carry_out, soma1bit_9_out, soma1bit_10_carry_out, soma1bit_10_out,
       soma1bit_11_carry_out, soma1bit_11_out, soma1bit_12_carry_out, soma1bit_12_out, soma1bit_13_carry_out,
       soma1bit_14_carry_out, soma1bit_14_out, soma1bit_15_carry_out, soma1bit_15_out, soma1bit_16_carry_out,
       soma1bit_16_out, soma1bit_17_carry_out, soma1bit_17_out, soma1bit_18_carry_out, soma1bit_19_carry_out,
       soma1bit_19_out, soma1bit_20_carry_out, soma1bit_20_out, soma1bit_21_carry_out, soma1bit_21_out,
       soma1bit_22_carry_out, soma1bit_23_carry_out, soma1bit_23_out, soma1bit_24_carry_out, soma1bit_24_out,
       soma1bit_25_carry_out, soma1bit_25_out, soma1bit_26_carry_out, soma1bit_27_carry_out,
       soma1bit_28_carry_out;

  or or_1 (Overflow, soma1bit_1_carry_out, soma1bit_2_carry_out, soma1bit_3_carry_out, soma1bit_4_carry_out, soma1bit_5_carry_out, soma1bit_6_carry_out, soma1bit_7_carry_out);
  and and_1 (and_1_out, In[7], In_2[0]);
  and and_2 (and_2_out, In[6], In_2[1]);
  Soma1bit soma1bit_1 (
    .Bit1(and_2_out), .Bit2(and_1_out), .Out(soma1bit_1_out), .Carry_In(soma1bit_8_carry_out),
    .Carry_Out(soma1bit_1_carry_out));
  and and_3 (and_3_out, In[5], In_2[2]);
  Soma1bit soma1bit_2 (
    .Bit1(and_3_out), .Bit2(soma1bit_1_out), .Out(soma1bit_2_out), .Carry_In(soma1bit_9_carry_out),
    .Carry_Out(soma1bit_2_carry_out));
  and and_4 (and_4_out, In[4], In_2[3]);
  Soma1bit soma1bit_3 (
    .Bit1(and_4_out), .Bit2(soma1bit_2_out), .Out(soma1bit_3_out), .Carry_In(soma1bit_10_carry_out),
    .Carry_Out(soma1bit_3_carry_out));
  and and_5 (and_5_out, In[3], In_2[4]);
  Soma1bit soma1bit_4 (
    .Bit1(and_5_out), .Bit2(soma1bit_3_out), .Out(soma1bit_4_out), .Carry_In(soma1bit_11_carry_out),
    .Carry_Out(soma1bit_4_carry_out));
  and and_6 (and_6_out, In[2], In_2[5]);
  Soma1bit soma1bit_5 (
    .Bit1(and_6_out), .Bit2(soma1bit_4_out), .Out(soma1bit_5_out), .Carry_In(soma1bit_12_carry_out),
    .Carry_Out(soma1bit_5_carry_out));
  and and_7 (and_7_out, In[1], In_2[6]);
  Soma1bit soma1bit_6 (
    .Bit1(and_7_out), .Bit2(soma1bit_5_out), .Out(soma1bit_6_out), .Carry_In(soma1bit_13_carry_out),
    .Carry_Out(soma1bit_6_carry_out));
  and and_8 (and_8_out, In[0], In_2[7]);
  Soma1bit soma1bit_7 (
    .Bit1(and_8_out), .Bit2(soma1bit_6_out), .Out(out_4[7]), .Carry_In(1'b0), .Carry_Out(soma1bit_7_carry_out));
  and and_9 (and_9_out, In[6], In_2[0]);
  and and_10 (and_10_out, In[5], In_2[1]);
  Soma1bit soma1bit_8 (
    .Bit1(and_10_out), .Bit2(and_9_out), .Out(soma1bit_8_out), .Carry_In(soma1bit_14_carry_out),
    .Carry_Out(soma1bit_8_carry_out));
  and and_11 (and_11_out, In[4], In_2[2]);
  Soma1bit soma1bit_9 (
    .Bit1(and_11_out), .Bit2(soma1bit_8_out), .Out(soma1bit_9_out), .Carry_In(soma1bit_15_carry_out),
    .Carry_Out(soma1bit_9_carry_out));
  and and_12 (and_12_out, In[3], In_2[3]);
  Soma1bit soma1bit_10 (
    .Bit1(and_12_out), .Bit2(soma1bit_9_out), .Out(soma1bit_10_out), .Carry_In(soma1bit_16_carry_out),
    .Carry_Out(soma1bit_10_carry_out));
  and and_13 (and_13_out, In[2], In_2[4]);
  Soma1bit soma1bit_11 (
    .Bit1(and_13_out), .Bit2(soma1bit_10_out), .Out(soma1bit_11_out), .Carry_In(soma1bit_17_carry_out),
    .Carry_Out(soma1bit_11_carry_out));
  and and_14 (and_14_out, In[1], In_2[5]);
  Soma1bit soma1bit_12 (
    .Bit1(and_14_out), .Bit2(soma1bit_11_out), .Out(soma1bit_12_out), .Carry_In(soma1bit_18_carry_out),
    .Carry_Out(soma1bit_12_carry_out));
  and and_15 (and_15_out, In[0], In_2[6]);
  Soma1bit soma1bit_13 (
    .Bit1(and_15_out), .Bit2(soma1bit_12_out), .Out(out_4[6]), .Carry_In(1'b0),
    .Carry_Out(soma1bit_13_carry_out));
  and and_16 (and_16_out, In[5], In_2[0]);
  and and_17 (and_17_out, In[4], In_2[1]);
  Soma1bit soma1bit_14 (
    .Bit1(and_17_out), .Bit2(and_16_out), .Out(soma1bit_14_out), .Carry_In(soma1bit_19_carry_out),
    .Carry_Out(soma1bit_14_carry_out));
  and and_18 (and_18_out, In[3], In_2[2]);
  Soma1bit soma1bit_15 (
    .Bit1(and_18_out), .Bit2(soma1bit_14_out), .Out(soma1bit_15_out), .Carry_In(soma1bit_20_carry_out),
    .Carry_Out(soma1bit_15_carry_out));
  and and_19 (and_19_out, In[2], In_2[3]);
  Soma1bit soma1bit_16 (
    .Bit1(and_19_out), .Bit2(soma1bit_15_out), .Out(soma1bit_16_out), .Carry_In(soma1bit_21_carry_out),
    .Carry_Out(soma1bit_16_carry_out));
  and and_20 (and_20_out, In[1], In_2[4]);
  Soma1bit soma1bit_17 (
    .Bit1(and_20_out), .Bit2(soma1bit_16_out), .Out(soma1bit_17_out), .Carry_In(soma1bit_22_carry_out),
    .Carry_Out(soma1bit_17_carry_out));
  and and_21 (and_21_out, In[0], In_2[5]);
  Soma1bit soma1bit_18 (
    .Bit1(and_21_out), .Bit2(soma1bit_17_out), .Out(out_4[5]), .Carry_In(1'b0),
    .Carry_Out(soma1bit_18_carry_out));
  and and_22 (and_22_out, In[4], In_2[0]);
  and and_23 (and_23_out, In[3], In_2[1]);
  Soma1bit soma1bit_19 (
    .Bit1(and_23_out), .Bit2(and_22_out), .Out(soma1bit_19_out), .Carry_In(soma1bit_24_carry_out),
    .Carry_Out(soma1bit_19_carry_out));
  and and_24 (and_24_out, In[2], In_2[2]);
  Soma1bit soma1bit_20 (
    .Bit1(and_24_out), .Bit2(soma1bit_19_out), .Out(soma1bit_20_out), .Carry_In(soma1bit_25_carry_out),
    .Carry_Out(soma1bit_20_carry_out));
  and and_25 (and_25_out, In[1], In_2[3]);
  Soma1bit soma1bit_21 (
    .Bit1(and_25_out), .Bit2(soma1bit_20_out), .Out(soma1bit_21_out), .Carry_In(soma1bit_27_carry_out),
    .Carry_Out(soma1bit_21_carry_out));
  and and_26 (and_26_out, In[0], In_2[4]);
  Soma1bit soma1bit_22 (
    .Bit1(and_26_out), .Bit2(soma1bit_21_out), .Out(out_4[4]), .Carry_In(1'b0),
    .Carry_Out(soma1bit_22_carry_out));
  and and_27 (and_27_out, In[3], In_2[0]);
  and and_28 (and_28_out, In[2], In_2[0]);
  and and_29 (and_29_out, In[2], In_2[1]);
  and and_30 (and_30_out, In[1], In_2[1]);
  Soma1bit soma1bit_23 (
    .Bit1(and_30_out), .Bit2(and_28_out), .Out(soma1bit_23_out), .Carry_In(soma1bit_28_carry_out),
    .Carry_Out(soma1bit_23_carry_out));
  Soma1bit soma1bit_24 (
    .Bit1(and_29_out), .Bit2(and_27_out), .Out(soma1bit_24_out), .Carry_In(soma1bit_23_carry_out),
    .Carry_Out(soma1bit_24_carry_out));
  and and_31 (and_31_out, In[1], In_2[2]);
  and and_32 (and_32_out, In[0], In_2[2]);
  Soma1bit soma1bit_25 (
    .Bit1(and_31_out), .Bit2(soma1bit_24_out), .Out(soma1bit_25_out), .Carry_In(soma1bit_26_carry_out),
    .Carry_Out(soma1bit_25_carry_out));
  Soma1bit soma1bit_26 (
    .Bit1(and_32_out), .Bit2(soma1bit_23_out), .Out(out_4[2]), .Carry_In(1'b0),
    .Carry_Out(soma1bit_26_carry_out));
  and and_33 (and_33_out, In[0], In_2[3]);
  Soma1bit soma1bit_27 (
    .Bit1(and_33_out), .Bit2(soma1bit_25_out), .Out(out_4[3]), .Carry_In(1'b0),
    .Carry_Out(soma1bit_27_carry_out));
  and and_34 (and_34_out, In[1], In_2[0]);
  and and_35 (and_35_out, In[0], In_2[1]);
  Soma1bit soma1bit_28 (
    .Bit1(and_35_out), .Bit2(and_34_out), .Out(out_4[1]), .Carry_In(1'b0), .Carry_Out(soma1bit_28_carry_out));
  and and_36 (out_4[0], In[0], In_2[0]);
endmodule
